// Logisim project circuit.circ as structural Verilog: 1 circuit, main circuit main
module main (
);

  wire and_1_out, and_2_out, and_3_out, and_4_out, and_5_out, and_6_out, and_7_out, and_8_out, and_9_out,
       and_10_out, and_11_out, and_12_out, and_13_out, and_14_out, and_15_out, and_16_out, and_17_out,
       and_18_out, and_19_out, and_20_out, and_21_out, and_22_out, and_23_out, and_24_out, and_25_out,
       and_26_out, and_27_out, and_28_out, and_29_out, and_30_out, and_31_out, and_32_out, not_1_out,
       not_2_out, not_3_out, not_4_out, not_5_out, or_1_out, or_2_out, undriven, undriven_2, undriven_3,
       undriven_4, undriven_5;

  not not_1 (not_1_out, undriven);
  not not_2 (not_2_out, undriven_2);
  not not_3 (not_3_out, undriven_3);
  not not_4 (not_4_out, undriven_4);
  not not_5 (not_5_out, undriven_5);
  and and_1 (and_1_out, not_5_out, not_4_out, undriven_3, undriven_2, not_1_out);
  and and_2 (and_2_out, not_5_out, undriven_4, not_3_out, not_2_out, undriven);
  and and_3 (and_3_out, undriven_5, undriven_4, not_3_out, not_2_out, undriven);
  and and_4 (and_4_out, not_5_out, undriven_4, not_3_out, not_2_out, not_1_out);
  and and_5 (and_5_out, not_5_out, not_4_out, not_3_out, undriven_2, not_1_out);
  and and_6 (and_6_out, not_5_out, not_4_out, not_3_out, not_2_out, undriven);
  and and_7 (and_7_out, not_5_out, not_4_out, undriven_3, not_2_out, not_1_out);
  and and_8 (and_8_out, undriven_5, undriven_4, undriven_3, undriven_2, not_1_out);
  and and_9 (and_9_out, not_5_out, undriven_4, not_3_out, undriven_2, not_1_out);
  and and_10 (and_10_out, not_5_out, not_4_out, undriven_3, not_2_out, undriven);
  and and_11 (and_11_out, undriven_5, not_4_out, not_3_out, not_2_out, not_1_out);
  and and_12 (and_12_out, not_5_out, not_4_out, not_3_out, undriven_2, undriven);
  and and_13 (and_13_out, undriven_5, not_4_out, undriven_3, undriven_2, not_1_out);
  and and_14 (and_14_out, not_5_out, not_4_out, undriven_3, undriven_2, undriven);
  and and_15 (and_15_out, undriven_5, undriven_4, not_3_out, not_2_out, not_1_out);
  and and_16 (and_16_out, not_5_out, undriven_4, undriven_3, not_2_out, undriven);
  and and_17 (and_17_out, undriven_5, not_4_out, undriven_3, undriven_2, undriven);
  and and_18 (and_18_out, undriven_5, not_4_out, undriven_3, not_2_out, not_1_out);
  and and_19 (and_19_out, not_5_out, undriven_4, undriven_3, undriven_2, undriven);
  and and_20 (and_20_out, undriven_5, undriven_4, undriven_3, not_2_out, not_1_out);
  or or_1 (or_1_out, and_5_out, and_11_out);
  and and_21 (and_21_out, undriven_5, not_4_out, not_3_out, not_2_out, undriven);
  and and_22 (and_22_out, undriven_5, undriven_4, undriven_3, undriven_2, undriven);
  and and_23 (and_23_out, not_5_out, not_4_out, not_3_out, not_2_out, not_1_out);
  and and_24 (and_24_out, undriven_5, not_4_out, not_3_out, undriven_2, not_1_out);
  and and_25 (and_25_out, undriven_5, not_4_out, not_3_out, undriven_2, undriven);
  and and_26 (and_26_out, undriven_5, undriven_4, not_3_out, undriven_2, undriven);
  and and_27 (and_27_out, undriven_5, undriven_4, not_3_out, undriven_2, not_1_out);
  and and_28 (and_28_out, not_5_out, undriven_4, not_3_out, undriven_2, undriven);
  or or_2 (or_2_out, and_6_out, and_7_out);
  and and_29 (and_29_out, undriven_5, undriven_4, undriven_3, not_2_out, undriven);
  and and_30 (and_30_out, not_5_out, undriven_4, undriven_3, undriven_2, not_1_out);
  and and_31 (and_31_out, undriven_5, not_4_out, undriven_3, not_2_out, undriven);
  and and_32 (and_32_out, not_5_out, undriven_4, undriven_3, not_2_out, not_1_out);
  // OR_Gate or_3 has open pins: in0=and_23_out, in1=or_1_out, in2=and_4_out, in3=and_18_out, in4=and_32_out, in5=and_20_out, in6=and_24_out, in7=and_9_out, in8=and_27_out, in9=and_1_out, in10=and_13_out, in11=and_30_out, in12=and_2_out, out=open
  // OR_Gate or_4 has open pins: in0=and_23_out, in1=or_1_out, in2=and_4_out, in3=and_15_out, in4=or_2_out, in5=and_32_out, in6=and_20_out, in7=and_24_out, in8=and_9_out, in9=and_27_out, in10=and_1_out, in11=and_13_out, in12=and_8_out, in13=and_21_out, in14=and_2_out, out=open
  // OR_Gate or_5 has open pins: in0=and_23_out, in1=and_15_out, in2=or_2_out, in3=and_18_out, in4=and_20_out, in5=and_24_out, in6=and_27_out, in7=and_1_out, in8=and_30_out, in9=and_8_out, in10=and_21_out, in11=and_2_out, out=open
  // OR_Gate or_6 has open pins: in0=and_4_out, in1=and_18_out, in2=and_24_out, in3=or_2_out, in4=and_1_out, in5=and_13_out, in6=and_8_out, in7=and_21_out, in8=and_2_out, out=open
  // OR_Gate or_7 has open pins: in0=or_1_out, in1=and_18_out, in2=and_20_out, in3=or_1_out, in4=and_9_out, in5=and_30_out, in6=and_8_out, in7=and_21_out, in8=and_2_out, out=open
  // OR_Gate or_8 has open pins: in0=and_23_out, in1=or_1_out, in2=and_18_out, in3=and_32_out, in4=and_24_out, in5=and_9_out, in6=and_27_out, in7=and_1_out, in8=and_13_out, out=open
  // OR_Gate or_9 has open pins: in0=and_23_out, in1=and_4_out, in2=and_15_out, in3=or_2_out, in4=and_18_out, in5=and_32_out, in6=and_24_out, in7=and_9_out, in8=and_13_out, in9=and_8_out, in10=and_2_out, out=open
endmodule
